// Logisim project Arquivos-logisim.circ as structural Verilog: 7 circuits, main circuit quest-1a
module quest_1a (
  input  a,
  input  b,
  output x
);

  wire NOT_2_out, NOT_out, OR_out;

  not NOT (NOT_out, a);
  not NOT_2 (NOT_2_out, b);
  or OR (OR_out, NOT_out, NOT_2_out);
  not NOT_3 (x, OR_out);
endmodule

module quest_1b (
  input  a,
  input  b,
  output x
);

  wire AND_out, NOT_2_out, NOT_out;

  not NOT (NOT_out, a);
  not NOT_2 (NOT_2_out, b);
  and AND (AND_out, NOT_out, NOT_2_out);
  not NOT_3 (x, AND_out);
endmodule

module quest_2a (
  input  A,
  input  B,
  input  C,
  output T
);

  wire AND_2_out, AND_3_out, AND_out;

  and AND (AND_out, A, B);
  and AND_2 (AND_2_out, A, C);
  and AND_3 (AND_3_out, B, C);
  or OR (T, AND_out, AND_2_out, AND_3_out);
endmodule

module quest_2b (
  input  A,
  input  B,
  input  C,
  output S
);

  wire AND_2_out, AND_3_out, AND_4_out, AND_out, not_2_out, not_3_out, not_4_out, not_5_out, not_6_out,
       NOT_out;

  not NOT (NOT_out, A);
  not not_2 (not_2_out, B);
  not not_3 (not_3_out, A);
  not not_4 (not_4_out, C);
  not not_5 (not_5_out, B);
  not not_6 (not_6_out, C);
  and AND (AND_out, NOT_out, not_2_out, C);
  and AND_2 (AND_2_out, not_3_out, B, not_4_out);
  and AND_3 (AND_3_out, A, not_5_out, not_6_out);
  and AND_4 (AND_4_out, A, B, C);
  or OR (S, AND_out, AND_2_out, AND_3_out, AND_4_out);
endmodule

module quest_3a (
  input  A,
  input  B,
  input  C,
  output T
);

  wire nand_1_out, nand_2_out, nand_3_out;

  nand nand_1 (nand_1_out, A, B);
  nand nand_2 (nand_2_out, A, C);
  nand nand_3 (nand_3_out, B, C);
  nand nand_4 (T, nand_1_out, nand_2_out, nand_3_out);
endmodule

module quest_3b (
  input  A,
  input  B,
  input  C,
  output S
);

  wire nand_1_out, nand_2_out, nand_3_out, nand_4_out, nand_5_out, nand_6_out, nand_7_out, nand_8_out,
       nand_9_out, nand_10_out;

  nand nand_1 (nand_1_out, A, A);
  nand nand_2 (nand_2_out, B, B);
  nand nand_3 (nand_3_out, A, A);
  nand nand_4 (nand_4_out, C, C);
  nand nand_5 (nand_5_out, B, B);
  nand nand_6 (nand_6_out, C, C);
  nand nand_7 (nand_7_out, nand_1_out, nand_2_out, C);
  nand nand_8 (nand_8_out, nand_3_out, B, nand_4_out);
  nand nand_9 (nand_9_out, A, nand_5_out, nand_6_out);
  nand nand_10 (nand_10_out, A, B, C);
  nand nand_11 (S, nand_7_out, nand_8_out, nand_9_out, nand_10_out);
endmodule

module quest_4 (
  input  D0,
  input  D1,
  input  D2,
  input  D3,
  input  S1,
  input  S0,
  output Y
);

  wire nand_1_out, nand_2_out, nand_3_out, nand_4_out, nand_5_out, nand_6_out, nand_7_out, nand_8_out;

  nand nand_1 (nand_1_out, S1, S1);
  nand nand_2 (nand_2_out, S0, S0);
  nand nand_3 (nand_3_out, S1, S1);
  nand nand_4 (nand_4_out, S0, S0);
  nand nand_5 (nand_5_out, D0, nand_1_out, nand_2_out);
  nand nand_6 (nand_6_out, D1, nand_3_out, S0);
  nand nand_7 (nand_7_out, D2, S1, nand_4_out);
  nand nand_8 (nand_8_out, D3, S1, S0);
  nand nand_9 (Y, nand_5_out, nand_6_out, nand_7_out, nand_8_out);
endmodule
