// Logisim project multi4x1.circ as structural Verilog: 2 circuits, main circuit main
module main (
  input  D3,
  input  D2,
  input  D1,
  input  D0,
  input  [2:0] S,
  input  D4,
  input  D5,
  input  D6,
  input  D7,
  output Y
);

  wire multiplexer_1_out, multiplexer_2_out;
  wire [1:0] bit_extender_1_out;

  Multiplexer #(.select(2)) multiplexer_1 (
    .in0(D0), .in1(D1), .in2(D2), .in3(D3), .out(multiplexer_1_out), .sel(S[1:0]));  // open: en
  Multiplexer #(.select(2)) multiplexer_2 (
    .in0(D4), .in1(D5), .in2(D6), .in3(D7), .out(multiplexer_2_out), .sel(S[1:0]));  // open: en
  Multiplexer #(.select(2)) multiplexer_3 (
    .in0(multiplexer_1_out), .in1(multiplexer_2_out), .out(Y), .sel(bit_extender_1_out));  // open: in2, in3, en
  assign bit_extender_1_out = {{1{1'b0}}, S[2]};  // Bit_Extender bit_extender_1
endmodule

module teste2 (
  input  D0,
  input  D1,
  input  D2,
  input  D3,
  input  D4,
  input  [2:0] S0S1S2,
  input  D5,
  input  D6,
  input  D7,
  output Y
);

  Multiplexer #(.select(3)) multiplexer_1 (
    .in0(D0), .in1(D1), .in2(D2), .in3(D3), .in4(D4), .in5(D5), .in6(D6), .in7(D7), .out(Y), .sel(S0S1S2));  // open: en
endmodule
